// Logisim project TallerLogica-Combinatorios.circ as structural Verilog: 16 circuits, main circuit verificador
module sumador_simple (
  input  A,
  input  B,
  output S,
  output Cout
);

  and and_1 (Cout, A, B);
  xor xor_1 (S, A, B);
endmodule

module sumador_completo (
  input  Cin,
  input  A,
  input  B,
  output S,
  output Cout
);

  wire sumador_simple_1_cout, sumador_simple_1_s, sumador_simple_2_cout;

  sumador_simple sumador_simple_1 (.A(A), .B(B), .S(sumador_simple_1_s), .Cout(sumador_simple_1_cout));
  sumador_simple sumador_simple_2 (.A(Cin), .B(sumador_simple_1_s), .S(S), .Cout(sumador_simple_2_cout));
  or or_1 (Cout, sumador_simple_2_cout, sumador_simple_1_cout);
endmodule

module sumador_4 (
  input  Cin,
  input  [3:0] A,
  input  [3:0] B,
  output [3:0] S,
  output Cout
);

  wire sumador_completo_1_cout, sumador_completo_2_cout, sumador_completo_3_cout;

  sumador_completo sumador_completo_1 (.Cin(Cin), .A(A[0]), .B(B[0]), .S(S[0]), .Cout(sumador_completo_1_cout));
  sumador_completo sumador_completo_2 (
    .Cin(sumador_completo_1_cout), .A(A[1]), .B(B[1]), .S(S[1]), .Cout(sumador_completo_2_cout));
  sumador_completo sumador_completo_3 (
    .Cin(sumador_completo_2_cout), .A(A[2]), .B(B[2]), .S(S[2]), .Cout(sumador_completo_3_cout));
  sumador_completo sumador_completo_4 (.Cin(sumador_completo_3_cout), .A(A[3]), .B(B[3]), .S(S[3]), .Cout(Cout));
  Hex_Digit_Display hex_digit_display_1 (.value(S));  // open: dp
endmodule

module comparador_cero (
  input  [3:0] A,
  output Z
);

  wire or_1_out, or_2_out, or_3_out;

  or or_1 (or_1_out, A[0], A[1]);
  or or_2 (or_2_out, or_1_out, A[2]);
  or or_3 (or_3_out, or_2_out, A[3]);
  not not_1 (Z, or_3_out);
endmodule

module sumador_flags (
  input  Cin,
  input  [3:0] A,
  input  [3:0] B,
  output [3:0] S,
  output N,
  output Z,
  output V,
  output C
);

  wire sumador_completo_1_cout, sumador_completo_2_cout, sumador_completo_3_cout, sumador_completo_4_cout;

  sumador_completo sumador_completo_1 (.Cin(Cin), .A(A[0]), .B(B[0]), .Cout(sumador_completo_1_cout));  // open: S
  sumador_completo sumador_completo_2 (
    .Cin(sumador_completo_1_cout), .A(A[1]), .B(B[1]), .Cout(sumador_completo_2_cout));  // open: S
  sumador_completo sumador_completo_3 (
    .Cin(sumador_completo_2_cout), .A(A[2]), .B(B[2]), .Cout(sumador_completo_3_cout));  // open: S
  sumador_4 sumador_4_1 (.Cin(Cin), .A(A), .B(B), .S({N, S[2:0]}), .Cout(C));
  Hex_Digit_Display hex_digit_display_1 (.value({N, S[2:0]}));  // open: dp
  sumador_completo sumador_completo_4 (
    .Cin(sumador_completo_3_cout), .A(A[3]), .B(B[3]), .Cout(sumador_completo_4_cout));  // open: S
  comparador_cero comparador_cero_1 (.A({N, S[2:0]}), .Z(Z));
  xor xor_1 (V, sumador_completo_3_cout, sumador_completo_4_cout);

  assign S[3] = N;
endmodule

module incrementador_4 (
  input  [3:0] A,
  output [3:0] S
);

  Hex_Digit_Display hex_digit_display_1 (.value(A));  // open: dp
  sumador_4 sumador_4_1 (.A(A), .B(4'b0001), .S(S));  // open: Cin, Cout
  Hex_Digit_Display hex_digit_display_2 (.value(S));  // open: dp
endmodule

module inversor_4 (
  input  [3:0] A,
  input  INV,
  output [3:0] S
);

  wire [3:0] inv_1_1_s;

  inv_1 inv_1_1 (.A(A), .INV(INV), .S(inv_1_1_s));
  Hex_Digit_Display hex_digit_display_1 (.value(S));  // open: dp
  incrementador_4 incrementador_4_1 (.A(inv_1_1_s), .S(S));
endmodule

module ALU (
  input  [3:0] A,
  input  [3:0] B,
  input  [1:0] OP,
  output N,
  output Z,
  output V,
  output C,
  output [3:0] S
);

  wire comparador_cero_1_z, comparador_cero_2_z, multiplexer_2_out, multiplexer_3_out, multiplexer_5_out,
       multiplexer_6_out, multiplexer_7_out, multiplexer_8_out, RESTA_bout, RESTA_n, RESTA_v, RESTA_z,
       SUMA_c, SUMA_n, SUMA_v, SUMA_z;
  wire [3:0] A_AND_B_s, A_OR_B_s, multiplexer_1_out, multiplexer_4_out, RESTA_s, SUMA_s;

  Hex_Digit_Display hex_digit_display_1 (.value(B));  // open: dp
  Hex_Digit_Display hex_digit_display_2 (.value(A));  // open: dp
  and_4 A_AND_B (.A(A), .B(B), .S(A_AND_B_s));
  or_4 A_OR_B (.A(A), .B(B), .S(A_OR_B_s));
  Hex_Digit_Display hex_digit_display_3 (.value(A_AND_B_s));  // open: dp
  Hex_Digit_Display hex_digit_display_4 (.value(A_OR_B_s));  // open: dp
  sumador_flags SUMA (.A(A), .B(B), .S(SUMA_s), .N(SUMA_n), .Z(SUMA_z), .V(SUMA_v), .C(SUMA_c));  // open: Cin
  resta_flags RESTA (.A(A), .B(B), .S(RESTA_s), .N(RESTA_n), .Z(RESTA_z), .V(RESTA_v), .Bout(RESTA_bout));  // open: Bin
  Hex_Digit_Display hex_digit_display_5 (.value(SUMA_s));  // open: dp
  Multiplexer #(.width(4)) multiplexer_1 (.in0(A_AND_B_s), .in1(A_OR_B_s), .out(multiplexer_1_out), .sel(OP[0]));
  Hex_Digit_Display hex_digit_display_6 (.value(RESTA_s));  // open: dp
  comparador_cero comparador_cero_1 (.A(A_AND_B_s), .Z(comparador_cero_1_z));
  comparador_cero comparador_cero_2 (.A(A_OR_B_s), .Z(comparador_cero_2_z));
  Multiplexer multiplexer_2 (.in0(SUMA_n), .in1(RESTA_n), .out(multiplexer_2_out), .sel(OP[0]));
  Multiplexer multiplexer_3 (
    .in0(comparador_cero_1_z), .in1(comparador_cero_2_z), .out(multiplexer_3_out), .sel(OP[0]));
  Multiplexer #(.width(4)) multiplexer_4 (.in0(SUMA_s), .in1(RESTA_s), .out(multiplexer_4_out), .sel(OP[0]));
  Multiplexer multiplexer_5 (.in0(SUMA_z), .in1(RESTA_z), .out(multiplexer_5_out), .sel(OP[0]));
  Multiplexer multiplexer_6 (.in0(SUMA_c), .in1(RESTA_bout), .out(multiplexer_6_out), .sel(OP[0]));
  Multiplexer multiplexer_7 (.in0(SUMA_v), .in1(RESTA_v), .out(multiplexer_7_out), .sel(OP[0]));
  Multiplexer multiplexer_8 (.in0(A_AND_B_s[3]), .in1(A_OR_B_s[3]), .out(multiplexer_8_out), .sel(OP[0]));
  Multiplexer multiplexer_9 (.in0(multiplexer_7_out), .in1(1'b0), .out(V), .sel(OP[1]));
  Multiplexer multiplexer_10 (.in0(multiplexer_6_out), .in1(1'b0), .out(C), .sel(OP[1]));
  Multiplexer multiplexer_11 (.in0(multiplexer_2_out), .in1(multiplexer_8_out), .out(N), .sel(OP[1]));
  Multiplexer multiplexer_12 (.in0(multiplexer_5_out), .in1(multiplexer_3_out), .out(Z), .sel(OP[1]));
  Multiplexer #(.width(4)) multiplexer_13 (.in0(multiplexer_4_out), .in1(multiplexer_1_out), .out(S), .sel(OP[1]));
  Hex_Digit_Display hex_digit_display_7 (.value(S));  // open: dp

  // Notes on the sheet:
  //   S_AND_OR
  //   Z_AND_OR
  //   0_AND_OR
  //   N_AND_OR
endmodule

module verificador (
  output [3:0] out_1,
  output [3:0] out_2,
  output [1:0] out_3,
  output halt,
  output N,
  output Z,
  output V,
  output C,
  output [3:0] res
);

  wire clock_1_out;

  Clock clock_1 (.out(clock_1_out));
  Counter #(.max('h3ff), .width(10)) counter_1 (
    .clk(clock_1_out), .carry(halt), .Q({out_3, out_2, out_1}));  // open: clr, load, up, count, D
  ALU alu_1 (.A(out_1), .B(out_2), .OP(out_3), .N(N), .Z(Z), .V(V), .C(C), .S(res));
endmodule

module resta_simple (
  input  A,
  input  B,
  output S,
  output Bout
);

  xor xor_1 (S, A, B);
  and and_1 (Bout, B, S);
endmodule

module resta_completa (
  input  Bin,
  input  A,
  input  B,
  output S,
  output Bout
);

  wire resta_simple_1_bout, resta_simple_1_s, resta_simple_2_bout;

  resta_simple resta_simple_1 (.A(A), .B(Bin), .S(resta_simple_1_s), .Bout(resta_simple_1_bout));
  resta_simple resta_simple_2 (.A(resta_simple_1_s), .B(B), .S(S), .Bout(resta_simple_2_bout));
  or or_1 (Bout, resta_simple_1_bout, resta_simple_2_bout);
endmodule

module resta_4 (
  input  Bin,
  input  [3:0] A,
  input  [3:0] B,
  output [3:0] S,
  output Bout
);

  wire resta_completa_1_bout, resta_completa_2_bout, resta_completa_3_bout;

  resta_completa resta_completa_1 (.Bin(Bin), .A(A[0]), .B(B[0]), .S(S[0]), .Bout(resta_completa_1_bout));
  resta_completa resta_completa_2 (
    .Bin(resta_completa_1_bout), .A(A[1]), .B(B[1]), .S(S[1]), .Bout(resta_completa_2_bout));
  resta_completa resta_completa_3 (
    .Bin(resta_completa_2_bout), .A(A[2]), .B(B[2]), .S(S[2]), .Bout(resta_completa_3_bout));
  resta_completa resta_completa_4 (.Bin(resta_completa_3_bout), .A(A[3]), .B(B[3]), .S(S[3]), .Bout(Bout));
  Hex_Digit_Display hex_digit_display_1 (.value(S));  // open: dp
endmodule

module inv_1 (
  input  [3:0] A,
  input  INV,
  output [3:0] S
);

  xor xor_1 (S[0], A[0], INV);
  xor xor_2 (S[1], A[1], INV);
  xor xor_3 (S[2], A[2], INV);
  xor xor_4 (S[3], A[3], INV);
  Hex_Digit_Display hex_digit_display_1 (.value(S));  // open: dp
endmodule

module resta_flags (
  input  Bin,
  input  [3:0] A,
  input  [3:0] B,
  output [3:0] S,
  output N,
  output Z,
  output V,
  output Bout
);

  wire resta_completa_1_bout, resta_completa_2_bout, resta_completa_3_bout, resta_completa_4_bout;

  resta_completa resta_completa_1 (.Bin(Bin), .A(A[0]), .B(B[0]), .Bout(resta_completa_1_bout));  // open: S
  resta_completa resta_completa_2 (
    .Bin(resta_completa_1_bout), .A(A[1]), .B(B[1]), .Bout(resta_completa_2_bout));  // open: S
  resta_completa resta_completa_3 (
    .Bin(resta_completa_2_bout), .A(A[2]), .B(B[2]), .Bout(resta_completa_3_bout));  // open: S
  Hex_Digit_Display hex_digit_display_1 (.value({N, S[2:0]}));  // open: dp
  resta_4 resta_4_1 (.Bin(Bin), .A(A), .B(B), .S({N, S[2:0]}), .Bout(Bout));
  resta_completa resta_completa_4 (
    .Bin(resta_completa_3_bout), .A(A[3]), .B(B[3]), .Bout(resta_completa_4_bout));  // open: S
  comparador_cero comparador_cero_1 (.A({N, S[2:0]}), .Z(Z));
  xor xor_1 (V, resta_completa_3_bout, resta_completa_4_bout);

  assign S[3] = N;
endmodule

module and_4 (
  input  [3:0] A,
  input  [3:0] B,
  output [3:0] S
);

  and and_1 (S[0], A[0], B[0]);
  and and_2 (S[1], A[1], B[1]);
  and and_3 (S[2], A[2], B[2]);
  and and_4 (S[3], A[3], B[3]);
  Hex_Digit_Display hex_digit_display_1 (.value(S));  // open: dp
endmodule

module or_4 (
  input  [3:0] A,
  input  [3:0] B,
  output [3:0] S
);

  or or_1 (S[0], A[0], B[0]);
  or or_2 (S[1], A[1], B[1]);
  or or_3 (S[2], A[2], B[2]);
  or or_4 (S[3], A[3], B[3]);
  Hex_Digit_Display hex_digit_display_1 (.value(S));  // open: dp
endmodule
